// Digital circuit CPU.dig as structural Verilog
module CPU (
  input  CLK,
  input  [7:0] Input_8Bits,
  input  DBG_CLK1,
  input  DBG_CLK0,
  output [7:0] Output_8Bits,
  output [7:0] DBG_PC0,
  output [7:0] DBG_PC1,
  output Stack_OVERSIZE,
  output Stack_EMPTY,
  output [7:0] PC
);

  wire and_1_out, and_3_out, and_5_out, and_6_out, and_7_out, Branching_SetUp_q, comparator_1_eq,
       comparator_2_eq, comparator_4_lt, comparator_6_eq, comparator_7_eq, counterpreset_1_ovf, EX_Do_Jump,
       EX_DO_Stack, EX_Do_TAKE, EX_IMM_check, EX_Jump_EN, EX_Math_EN, EX_Mem_EN, EX_Mov_EN, EX_NO_NOP,
       EX_NOP_Out, ID_IMM_check, ME_Do_PSH, ME_Do_RD, ME_Do_ST, ME_Do_WR, multiplexer_3_out,
       multiplexer_7_out, multiplexer_10_out, multiplexer_20_out, not_4_out, not_5_out, not_8_out, not_9_out,
       not_10_out, not_13_out, not_14_out, not_17_out, not_18_out, not_19_out, not_20_out, not_21_out,
       NotNOPing, or_1_out, or_2_out, or_5_out, or_6_out, register_1_q, register_2_q, register_5_q,
       WB_Do_Jump_Prev, WB_EN, WB_EN_Prev;
  wire [1:0] counter_1_out, EX_Do_SMTH, multiplexer_4_out, not_2_out, not_3_out;
  wire [2:0] EX_ALU_Choice_01, EX_ALU_Choice_10, EX_R_Dest, EX_R_Src1, EX_R_Src2, ID_R_Dest, ID_R_Src1,
       ID_R_Src2, ME_R_Src2, ME_To_WB_R_Dest, multiplexer_9_out, multiplexer_16_out, WB_R_Dest;
  wire [3:0] ALU_c_f, EX_Reg_F;
  wire [4:0] ID_Opcode, multiplexer_13_out;
  wire [5:0] ME_WB_R_Dest_Out, rom_1_d;
  wire [6:5] ME_CMD_Out;
  wire [7:0] ALU_res, EX_ALU_Out, EX_Data_A, EX_Data_B, EX_Forward_A, EX_Forward_B, EX_ME_Stack_Addr,
       EX_ME_Stack_Out, ID_Data_A, ID_Data_B, ID_StackPtr_Out, ME_LD_ST_Out, ME_RD_WR_Out, multiplexer_1_out,
       multiplexer_2_out, multiplexer_14_out, not_6_out, not_7_out, not_11_out, not_12_out, R_Src_2_Out,
       WB_Data_Out;
  wire [7:3] ID_R_Src2_IMM;
  wire [8:0] ID_EX_Stack_Out;
  wire [10:0] ME_WB_CMD_Out;
  wire [15:0] EX_ME_Forward_Out, ME_WB_Data_Out, multiplexer_11_out;
  wire [15:8] ME_Data_Out;
  wire [17:0] PSH_POP_CMD;
  wire [18:0] multiplexer_5_out;
  wire [18:16] LD_ST_CMD;
  wire [19:0] Instruction_d;
  wire [24:24] ID_EX_Out;
  wire [25:0] multiplexer_19_out;
  wire [26:0] EX_ME_Out;

  nand nand_1 (NotNOPing, not_4_out, or_2_out);
  or or_1 (or_1_out, EX_Do_TAKE, comparator_1_eq);
  or or_2 (or_2_out, multiplexer_3_out, EX_Do_TAKE);
  Register Branching_SetUp (.D(or_2_out), .C(CLK), .en(or_1_out), .Q(Branching_SetUp_q));
  Demultiplexer #(.Selector_Bits(2)) demultiplexer_1 (
    .sel(EX_Do_SMTH), .in(EX_NO_NOP), .out_0(EX_Jump_EN), .out_1(EX_Math_EN), .out_2(EX_Mem_EN),
    .out_3(EX_Mov_EN));
  Multiplexer #(.Bits(8)) multiplexer_1 (.sel(EX_Mov_EN), .in_0(EX_ALU_Out), .in_1(EX_Data_B), .out(multiplexer_1_out));
  Multiplexer #(.Bits(8)) multiplexer_2 (
    .sel(ME_Do_RD), .in_0(R_Src_2_Out), .in_1(Input_8Bits), .out(multiplexer_2_out));
  Counter #(.Bits(2)) counter_1 (
    .en(Branching_SetUp_q), .C(CLK), .clr(comparator_1_eq), .out(counter_1_out));  // open: ovf
  not not_1 (EX_NO_NOP, ID_EX_Out[24]);
  and and_1 (and_1_out, CLK, EX_NO_NOP);
  Demultiplexer #(.Bits(3)) demultiplexer_2 (
    .sel(ME_Do_WR), .in(EX_ME_Out[18:16]), .out_0(ME_To_WB_R_Dest), .out_1(ME_R_Src2));
  Demultiplexer #(.Bits(8)) demultiplexer_3 (
    .sel(ME_Do_RD), .in(multiplexer_2_out), .out_0(Output_8Bits), .out_1(ME_RD_WR_Out));
  and and_2 (LD_ST_CMD[17], CLK, EX_ME_Out[20]);
  assign not_2_out = ~EX_Do_SMTH;  // Not not_2, 2 bits wide
  ROM #(.AddrBits(8), .Bits(20)) Instruction (.A(DBG_PC0), .sel(NotNOPing), .D(Instruction_d));
  Multiplexer multiplexer_3 (.sel(comparator_1_eq), .in_0(Branching_SetUp_q), .in_1(1'b0), .out(multiplexer_3_out));
  Comparator #(.Bits(2)) comparator_1 (.a(counter_1_out), .b(2'b10), .eq(comparator_1_eq));  // open: gt, lt
  assign not_3_out = ~not_2_out;  // Not not_3, 2 bits wide
  forward_register forward_register_1 (
    .Data_PostEX(multiplexer_1_out), .R_Dest_In(EX_R_Dest), .Do_SMTH(not_3_out), .CLK(and_1_out),
    .Data_1(EX_Data_A), .Data_2(EX_Data_B), .R_Src1(EX_R_Src1), .R_Src2(EX_R_Src2), .IMM_Check(EX_IMM_check),
    .Out_1(EX_Forward_A), .Out_2(EX_Forward_B));  // open: DBG1, DBG2, DBG3
  not not_4 (not_4_out, comparator_1_eq);
  Comparator #(.Bits(2)) comparator_2 (.a(EX_Do_SMTH), .b(2'b10), .eq(comparator_2_eq));  // open: gt, lt
  Comparator #(.Bits(2)) comparator_3 (.a(multiplexer_4_out), .b(2'b01), .gt(EX_DO_Stack));  // open: eq, lt
  Demultiplexer #(.Selector_Bits(2)) demultiplexer_4 (
    .sel(EX_ME_Out[20:19]), .in(EX_ME_Out[24]), .out_0(ME_Do_WR), .out_1(ME_Do_RD), .out_2(LD_ST_CMD[18]),
    .out_3(LD_ST_CMD[16]));
  Multiplexer #(.Bits(2)) multiplexer_4 (
    .sel(comparator_2_eq), .in_0(2'b00), .in_1({1'b1, EX_ALU_Choice_01[0]}), .out(multiplexer_4_out));
  Register #(.Bits(20)) IF_ID (
    .D(Instruction_d), .C(CLK), .en(1'b1),
    .Q({ID_Opcode, ID_IMM_check, ID_R_Dest, ID_R_Src1, ID_R_Src2_IMM, ID_R_Src2}));
  Multiplexer #(.Bits(19)) multiplexer_5 (
    .sel(EX_ME_Out[21]), .in_0({LD_ST_CMD, EX_ME_Forward_Out[7:0], EX_ME_Forward_Out[15:8]}),
    .in_1({LD_ST_CMD[18], PSH_POP_CMD[17], LD_ST_CMD[16], EX_ME_Forward_Out[15:8], PSH_POP_CMD[7:0]}),
    .out(multiplexer_5_out));
  and and_3 (and_3_out, EX_Jump_EN, EX_NO_NOP);
  and and_4 (PSH_POP_CMD[17], CLK, EX_ME_Out[20]);
  not not_5 (not_5_out, EX_Reg_F[3]);
  Multiplexer multiplexer_6 (.sel(and_3_out), .in_0(1'b0), .in_1(EX_Do_Jump), .out(EX_Do_TAKE));
  Demultiplexer demultiplexer_5 (.sel(EX_ME_Out[21]), .in(LD_ST_CMD[18]), .out_0(ME_CMD_Out[5]), .out_1(ME_CMD_Out[6]));
  Demultiplexer demultiplexer_6 (.sel(EX_ME_Out[21]), .in(LD_ST_CMD[16]), .out_0(ME_Do_ST), .out_1(ME_Do_PSH));
  assign not_6_out = ~multiplexer_5_out[7:0];  // Not not_6, 8 bits wide
  assign not_7_out = ~multiplexer_5_out[15:8];  // Not not_7, 8 bits wide
  not not_8 (not_8_out, multiplexer_5_out[16]);
  not not_9 (not_9_out, multiplexer_5_out[18]);
  Comparator #(.Bits(8)) comparator_4 (.a(8'h8), .b(ID_StackPtr_Out), .lt(comparator_4_lt));  // open: gt, eq
  Multiplexer #(.Selector_Bits(2)) multiplexer_7 (
    .sel(EX_ALU_Choice_01[1:0]), .in_0(EX_Reg_F[0]), .in_1(EX_Reg_F[3]), .in_2(not_5_out),
    .in_3(EX_Reg_F[2]), .out(multiplexer_7_out));
  not not_10 (not_10_out, EX_Do_Jump);
  assign not_11_out = ~not_6_out;  // Not not_11, 8 bits wide
  assign not_12_out = ~not_7_out;  // Not not_12, 8 bits wide
  not not_13 (not_13_out, not_8_out);
  not not_14 (not_14_out, not_9_out);
  assign PSH_POP_CMD[7:0] = ~EX_ME_Stack_Addr;  // Not not_15, 8 bits wide
  Multiplexer #(.Bits(8)) multiplexer_8 (
    .sel(EX_ME_Out[19]), .in_0(EX_ME_Stack_Out), .in_1(EX_ME_Stack_Out), .out(EX_ME_Stack_Addr));
  not not_16 (Stack_OVERSIZE, comparator_4_lt);
  and and_5 (and_5_out, not_10_out, and_3_out);
  Multiplexer #(.Bits(3)) multiplexer_9 (
    .sel(EX_Math_EN), .in_0(EX_ALU_Choice_10), .in_1(EX_ALU_Choice_01), .out(multiplexer_9_out));
  RAMDualPort #(.AddrBits(8), .Bits(8)) ramdualport_1 (
    .A(not_11_out), .Din(not_12_out), .str(not_13_out), .C(multiplexer_5_out[17]), .ld(not_14_out),
    .D(ME_LD_ST_Out));
  Register #(.Bits(8)) Stack (.D(EX_ALU_Out), .C(CLK), .en(EX_Mem_EN), .Q(ID_StackPtr_Out));
  Comparator #(.Bits(8)) comparator_5 (.a({8{1'b0}}), .b(ID_StackPtr_Out), .eq(Stack_EMPTY));  // open: gt, lt
  or or_3 (EX_Do_Jump, multiplexer_7_out, EX_ALU_Choice_01[2]);
  Multiplexer multiplexer_10 (.sel(and_5_out), .in_0(not_17_out), .in_1(EX_Jump_EN), .out(multiplexer_10_out));
  not not_17 (not_17_out, EX_NO_NOP);
  Multiplexer #(.Bits(16)) multiplexer_11 (
    .sel(EX_Math_EN), .in_0({8'h1, ID_EX_Stack_Out[7:0]}), .in_1({EX_Forward_B, EX_Forward_A}),
    .out(multiplexer_11_out));
  not not_18 (not_18_out, NotNOPing);
  or or_4 (EX_NOP_Out, EX_Do_TAKE, multiplexer_10_out);
  ALU ALU (
    .A(multiplexer_11_out[7:0]), .B(multiplexer_11_out[15:8]), .Do_Math(multiplexer_9_out), .Res(ALU_res),
    .C_F(ALU_c_f[0]), .O_F(ALU_c_f[1]), .N_F(ALU_c_f[2]), .Z_F(ALU_c_f[3]));
  Register register_1 (.D(EX_ME_Out[24]), .C(CLK), .en(1'b1), .Q(register_1_q));
  Register register_2 (.D(not_18_out), .C(CLK), .en(1'b1), .Q(register_2_q));
  Multiplexer #(.Bits(8)) multiplexer_12 (
    .sel(EX_ME_Out[20]), .in_0(ME_RD_WR_Out), .in_1(ME_LD_ST_Out), .out(ME_Data_Out));
  not not_19 (not_19_out, ME_WB_CMD_Out[10]);
  Multiplexer #(.Bits(5)) multiplexer_13 (.sel(or_5_out), .in_0(ID_Opcode), .in_1({5{1'b0}}), .out(multiplexer_13_out));
  or or_5 (or_5_out, not_18_out, register_2_q);
  and and_6 (and_6_out, EX_Math_EN, EX_NO_NOP);
  and and_7 (and_7_out, not_19_out, WB_EN);
  Multiplexer #(.Selector_Bits(2), .Bits(8)) multiplexer_14 (
    .sel(EX_Do_SMTH), .in_0({8{1'b0}}), .in_1(EX_ALU_Out), .in_2({8{1'b0}}), .in_3(EX_Data_B),
    .out(multiplexer_14_out));
  not not_20 (not_20_out, EX_DO_Stack);
  Multiplexer #(.Bits(8)) multiplexer_15 (.sel(not_20_out), .in_0({8{1'b0}}), .in_1(ALU_res), .out(EX_ALU_Out));
  Multiplexer #(.Bits(3)) multiplexer_16 (
    .sel(register_1_q), .in_0(ID_R_Src2), .in_1(ME_R_Src2), .out(multiplexer_16_out));
  Register #(.Bits(4)) register_3 (.D(ALU_c_f), .C(CLK), .en(and_6_out), .Q(EX_Reg_F));
  ROM #(.AddrBits(5), .Bits(6)) rom_1 (.A(multiplexer_13_out), .sel(1'b1), .D(rom_1_d));
  Multiplexer #(.Bits(8)) multiplexer_17 (
    .sel(ID_IMM_check), .in_0(R_Src_2_Out), .in_1({ID_R_Src2_IMM, ID_R_Src2}), .out(ID_Data_B));
  RegisterFile #(.AddrBits(3), .Bits(8)) RegFile (
    .Din(WB_Data_Out), .we(and_7_out), .Rw(WB_R_Dest), .C(CLK), .Ra(ID_R_Src1), .Rb(multiplexer_16_out),
    .Da(ID_Data_A), .Db(R_Src_2_Out));
  Comparator #(.Bits(2)) comparator_6 (.a(EX_Do_SMTH), .b(2'b10), .eq(comparator_6_eq));  // open: gt, lt
  Register #(.Bits(16)) ME_WB_Data (.D({ME_Data_Out, EX_ME_Out[7:0]}), .C(CLK), .en(1'b1), .Q(ME_WB_Data_Out));
  Register #(.Bits(6)) ME_WB_R_Dest (
    .D({EX_ME_Out[18:16], EX_ME_Out[18:16]}), .C(CLK), .en(1'b1), .Q(ME_WB_R_Dest_Out));
  Register #(.Bits(11)) ME_WB_CMD (
    .D({EX_ME_Out[25], EX_ME_Out[26], EX_ME_Out[21], EX_ME_Out[24], ME_CMD_Out, EX_ME_Out[23:19]}), .C(CLK),
    .en(1'b1), .Q(ME_WB_CMD_Out));
  Multiplexer #(.Bits(3)) multiplexer_18 (
    .sel(EX_ALU_Choice_01[0]), .in_0(3'b001), .in_1(3'b000), .out(EX_ALU_Choice_10));
  Multiplexer #(.Bits(26)) multiplexer_19 (
    .sel(comparator_6_eq),
    .in_0({EX_NOP_Out, 1'b0, EX_Do_SMTH, EX_ALU_Choice_01, EX_R_Dest, {8{1'b0}}, multiplexer_14_out}),
    .in_1({EX_NOP_Out, 1'b1, EX_Do_SMTH, EX_ALU_Choice_01, EX_R_Dest, EX_Data_A, EX_Data_B}),
    .out(multiplexer_19_out));
  or or_6 (or_6_out, ME_CMD_Out[5], ME_CMD_Out[6]);
  Register #(.Bits(2)) register_4 (
    .D({ME_WB_CMD_Out[7], ME_WB_CMD_Out[9]}), .C(CLK), .en(1'b1), .Q({WB_EN_Prev, WB_Do_Jump_Prev}));
  Comparator #(.Bits(2)) comparator_7 (.a(2'b10), .b(ME_WB_CMD_Out[4:3]), .eq(comparator_7_eq));  // open: gt, lt
  Multiplexer multiplexer_20 (
    .sel(ME_WB_CMD_Out[8]), .in_0(ME_WB_CMD_Out[7]), .in_1(WB_EN_Prev), .out(multiplexer_20_out));
  not not_21 (not_21_out, multiplexer_20_out);
  Register #(.Bits(9)) ID_EX_Stack (.D({Stack_EMPTY, ID_StackPtr_Out}), .C(CLK), .en(1'b1), .Q(ID_EX_Stack_Out));
  Register #(.Bits(32)) ID_EX (
    .D({ID_IMM_check, ID_R_Src2, ID_R_Src1, rom_1_d, ID_R_Dest, ID_Data_A, ID_Data_B}), .C(CLK), .en(1'b1),
    .Q({EX_IMM_check, EX_R_Src2, EX_R_Src1, ID_EX_Out[24], EX_Do_SMTH, EX_ALU_Choice_01, EX_R_Dest, EX_Data_A, EX_Data_B}));
  Register #(.Bits(27)) EX_ME (.D({EX_Do_Jump, multiplexer_19_out}), .C(CLK), .en(1'b1), .Q(EX_ME_Out));
  Register #(.Bits(16)) EX_ME_Forward (.D({EX_Forward_B, EX_Forward_A}), .C(CLK), .en(1'b1), .Q(EX_ME_Forward_Out));
  Register #(.Bits(8)) EX_ME_Stack (.D(ID_EX_Stack_Out[7:0]), .C(CLK), .en(1'b1), .Q(EX_ME_Stack_Out));
  Multiplexer #(.Bits(11)) multiplexer_21 (
    .sel(comparator_7_eq), .in_0({ME_WB_R_Dest_Out[2:0], ME_WB_Data_Out[7:0]}),
    .in_1({ME_WB_R_Dest_Out[5:3], ME_WB_Data_Out[15:8]}), .out({WB_R_Dest, WB_Data_Out}));
  or or_7 (WB_EN, not_21_out, register_5_q);
  Register register_5 (.D(or_6_out), .C(CLK), .en(1'b1), .Q(register_5_q));
  CounterPreset #(.Bits(8)) counterpreset_1 (
    .en(NotNOPing), .C(CLK), .dir(1'b0), .in(EX_Data_B), .ld(EX_Do_TAKE), .clr(counterpreset_1_ovf),
    .out(DBG_PC0), .ovf(counterpreset_1_ovf));
  Seven_Seg_Hex seven_seg_hex_1 (.d(Output_8Bits[7:4]), .dp(1'b0));
  Seven_Seg_Hex seven_seg_hex_2 (.d(Output_8Bits[3:0]), .dp(1'b0));

  assign DBG_PC1 = DBG_PC0;
  assign PC = DBG_PC0;

  // Other names for the same wires on the sheet: ID_R_Src2_IMM[2:0] = ID_R_Src2; CLK_Middle = DBG_CLK1;
  //   CLK_Upper = DBG_CLK0; LD_ST_CMD[15:0] = {EX_ME_Forward_Out[7:0], EX_ME_Forward_Out[15:8]};
  //   PSH_POP_CMD (some bits) = {LD_ST_CMD[18], LD_ST_CMD[16], EX_ME_Forward_Out[15:8]};
  //   ME_Data_B[7:0] = EX_ME_Out[7:0]; ME_Data_EX_Result[7:0] = EX_ME_Out[7:0]; ME_Data_Out[7:0] = EX_ME_Out[7:0];
  //   ME_Data_A[7:0] = EX_ME_Out[15:8]; ME_R_Dest[2:0] = EX_ME_Out[18:16]; ME_R_Dest_EX[2:0] = EX_ME_Out[18:16];
  //   ME_R_Dest_Out[5:0] = {EX_ME_Out[18:16], EX_ME_Out[18:16]};
  //   ME_CMD_Out (some bits) = {EX_ME_Out[25], EX_ME_Out[26], EX_ME_Out[21], EX_ME_Out[24:19]};
  //   ME_SMTH_Choice[2:0] = EX_ME_Out[21:19]; ME_RAM_EN = EX_ME_Out[20]; ME_PSH_POP_EN = EX_ME_Out[21];
  //   ME_Do_SMTH[1:0] = EX_ME_Out[23:22]; ME_EN = EX_ME_Out[24]; ME_WB_EN = EX_ME_Out[24]; ME_NOP = EX_ME_Out[25];
  //   ME_Do_Jump = EX_ME_Out[26]; ME_Do_Jump_EX = EX_ME_Out[26]; RegF_C = EX_Reg_F[0]; RegF_O = EX_Reg_F[1];
  //   RegF_N = EX_Reg_F[2]; RegF_Z = EX_Reg_F[3]; EX_StackPtr_Update = EX_Mem_EN; EX_MOV_Out[7:0] = EX_Data_B;
  //   ID_EX_Out (some bits) = {EX_IMM_check, EX_R_Src2, EX_R_Src1, EX_Do_SMTH, EX_ALU_Choice_01, EX_R_Dest, EX_Data_A, EX_Data_B};
  //   Line_Branch[7:0] = EX_Data_B; EX_SMTH_Choice[2:0] = EX_ALU_Choice_01; ID_Stack_EMPTY = Stack_EMPTY;
  //   ID_Stack_OVERSIZE = Stack_OVERSIZE; In_8bit[7:0] = Input_8Bits; ME_Do_LD = ME_CMD_Out[5];
  //   ME_Do_LD_POP = LD_ST_CMD[18]; ME_Do_POP = ME_CMD_Out[6]; ME_Do_ST_PSH = LD_ST_CMD[16];
  //   WB_SMTH_Choice[2:0] = ME_WB_CMD_Out[2:0]; WB_DO_SMTH[1:0] = ME_WB_CMD_Out[4:3]; WB_DO_LD = ME_WB_CMD_Out[5];
  //   WB_DO_POP = ME_WB_CMD_Out[6]; WB_EN_Curr = ME_WB_CMD_Out[7]; WB_PSH_POP_EN = ME_WB_CMD_Out[8];
  //   WB_Do_Jump_Curr = ME_WB_CMD_Out[9]; WB_NOP = ME_WB_CMD_Out[10]; WB_NOP_ME = ME_WB_CMD_Out[10];
  //   WB_Data_EX[7:0] = ME_WB_Data_Out[7:0]; WB_Data_ME[7:0] = ME_WB_Data_Out[15:8];
  //   WB_R_Dest_EX[2:0] = ME_WB_R_Dest_Out[2:0]; WB_R_Dest_ME[2:0] = ME_WB_R_Dest_Out[5:3];
  //   Out_8bits[7:0] = Output_8Bits; PC_Out[7:0] = DBG_PC0

  // Notes on the sheet:
  //   Pipeline Stages
  //   Instruction Fetch
  //   Execute
  //   Memory
  //   Branch Prediction
  //   Static Guess Not Taken Branch
  //   Data Forwarding Register
  //   Do_{I/O}
  //   Do_{LD/ST}
  //   Might be problem here
  //   Sol: change to 2 bits
  //   and detect for 10
  //   Opcode
  //   0000: LD
  //   0001: MOV
  //   0010: ST
  //   0011: RD
  //   0100: ADD
  //   0101L SUB
  //   0110: MUL
  //   0111: WR
  //   1000: AND
  //   1001: OR
  //   1010: XOR
  //   1011: NOT
  //   1100: BC
  //   1101:BZ
  //   1110: BNZ
  //   1111:B
  //   contents of Instruction (hex, n*v repeats v):
  //   f4043,9*b0000,14*b8001
  //   Do_{SMTH}: 10
  //   SMTH_{Choice}:
  //   000: RD
  //   001: WR
  //   IF/ID
  //   Do_{SMTH}: 10
  //   SMTH_{Choice}:
  //   010: LD
  //   011: ST
  //   Do_{Jump}
  //   Do_{PSH/POP}
  //   Do_{SMTH}: 00
  //   SMTH_{Choice}:
  //   000: BC
  //   001: BZ
  //   010: BNZ
  //   011: BNG
  //   100: B
  //   PSH: IN -> ChangePTR
  //   POP ChangePTR -> OUT
  //   Do_{Math}
  //   Do_{SMTH}: 01
  //   SMTH_{Choice}:
  //   000: ADD
  //   001: SUB
  //   010: MUL
  //   011: DC
  //   100:: AND
  //   101: Or
  //   110: XOR
  //   111: Not
  //   Instruction Decode
  //   Check if Stack is too big
  //   PC_{Out}
  //   Do_{SMTH}: 10
  //   SMTH_{Choice}:
  //   110: POP
  //   111: PSH
  //   CU
  //   NOP: [5]
  //   1: True
  //   0: False
  //   Do_{SMTH}: [4:3]
  //   00 Do_{Jump} (In:EX)
  //   01 Do_{Math}(In:EX -> WB)
  //   10 Do_{Mem} (In:ME -> WB)
  //   11 Do_{Mov} (In:WB)
  //   SMTH_{Choice}: [2:0]
  //   contents of rom_1 (hex, n*v repeats v):
  //   4*20,8,9,a,20,c,d,e,f,4*20,0,1,2,3,4,20,17,16,10,11,20,20,12,13
  //   ,18,20
  //   ME/WB
  //   Do_{Mem}
  //   Do_{SMTH}: 10
  //   SMTH_{Choice}:
  //   110: PSH
  //   111: POP
  //   ID/EX
  //   EX/ME
  //   Write Back
  //   Program Counter
  //   TODO:
  //   - Debug RD/WR
  //   - Debug PSH/POP
  //   OPTIONAL:
  //   - Implement SWI
endmodule
