// Digital circuit flag_register.dig as structural Verilog
module flag_register (
  input  [2:0] ONZ_i,
  input  Do_Write,
  output [2:0] ONZ_o
);

  D_flip_flop d_flip_flop_1 (.D(ONZ_i[0]), .CLK(Do_Write), .Q(ONZ_o[0]));  // open: Q_2
  D_flip_flop d_flip_flop_2 (.D(ONZ_i[1]), .CLK(Do_Write), .Q(ONZ_o[1]));  // open: Q_2
  D_flip_flop d_flip_flop_3 (.D(ONZ_i[2]), .CLK(Do_Write), .Q(ONZ_o[2]));  // open: Q_2
endmodule
