// Digital circuit forward_register.dig as structural Verilog
module forward_register (
  input  [7:0] Data_PostEX,
  input  [2:0] R_Dest_In,
  input  CLK,
  input  [7:0] Data_1,
  input  [7:0] Data_2,
  input  [2:0] R_Src1,
  input  [2:0] R_Src2,
  input  IMM_Check,
  input  [1:0] Do_SMTH,
  input  [2:0] SMTH_Choice,
  output [7:0] Out_1,
  output [7:0] Out_2,
  output [11:0] DBG1,
  output [11:0] DBG2,
  output [11:0] DBG3
);

  wire comparator_1_eq, comparator_2_eq, multiplexer_1_out;
  wire [2:0] comparator_3_eq, comparator_4_eq;
  wire [7:0] D_11, D_12, D_21, D_22, D_31, D_32, multiplexer_3_out, multiplexer_4_out, multiplexer_5_out,
       multiplexer_13_out;
  wire [11:0] multiplexer_2_out;

  Comparator #(.Bits(3)) comparator_1 (.a(SMTH_Choice), .b(3'b000), .eq(comparator_1_eq));  // open: gt, lt
  Comparator #(.Bits(2)) comparator_2 (.a(Do_SMTH), .b(2'b11), .eq(comparator_2_eq));  // open: gt, lt
  Multiplexer multiplexer_1 (.sel(comparator_2_eq), .in_0(Do_SMTH[0]), .in_1(comparator_1_eq), .out(multiplexer_1_out));
  Multiplexer #(.Bits(12)) multiplexer_2 (
    .sel(multiplexer_1_out), .in_0({12{1'b0}}), .in_1({1'b1, R_Dest_In, Data_PostEX}), .out(multiplexer_2_out));
  Register #(.Bits(12)) DataForward_Reg_1 (.D(multiplexer_2_out), .C(CLK), .en(multiplexer_1_out), .Q(DBG1));
  Register #(.Bits(12)) DataForward_Reg_2 (.D(DBG1), .C(CLK), .en(multiplexer_1_out), .Q(DBG2));
  Register #(.Bits(12)) DataForward_Reg_3 (.D(DBG2), .C(CLK), .en(multiplexer_1_out), .Q(DBG3));
  Multiplexer #(.Bits(8)) multiplexer_3 (.sel(DBG1[11]), .in_0(Data_1), .in_1(DBG1[7:0]), .out(multiplexer_3_out));
  Comparator #(.Bits(3)) comparator_3 (.a(DBG1[10:8]), .b(R_Src1), .eq(comparator_3_eq[2]));  // open: gt, lt
  Comparator #(.Bits(3)) comparator_4 (.a(DBG1[10:8]), .b(R_Src2), .eq(comparator_4_eq[2]));  // open: gt, lt
  Multiplexer #(.Bits(8)) multiplexer_4 (.sel(DBG2[11]), .in_0(Data_2), .in_1(DBG2[7:0]), .out(multiplexer_4_out));
  Comparator #(.Bits(3)) comparator_5 (.a(DBG2[10:8]), .b(R_Src1), .eq(comparator_3_eq[1]));  // open: gt, lt
  Comparator #(.Bits(3)) comparator_6 (.a(DBG2[10:8]), .b(R_Src2), .eq(comparator_4_eq[1]));  // open: gt, lt
  Multiplexer #(.Bits(8)) multiplexer_5 (.sel(DBG3[11]), .in_0({8{1'b1}}), .in_1(DBG3[7:0]), .out(multiplexer_5_out));
  Comparator #(.Bits(3)) comparator_7 (.a(DBG3[10:8]), .b(R_Src1), .eq(comparator_3_eq[0]));  // open: gt, lt
  Comparator #(.Bits(3)) comparator_8 (.a(DBG3[10:8]), .b(R_Src2), .eq(comparator_4_eq[0]));  // open: gt, lt
  Multiplexer #(.Bits(8)) multiplexer_6 (.sel(comparator_3_eq[2]), .in_0(Data_1), .in_1(multiplexer_3_out), .out(D_11));
  Multiplexer #(.Bits(8)) multiplexer_7 (.sel(comparator_4_eq[2]), .in_0(Data_2), .in_1(multiplexer_3_out), .out(D_12));
  Multiplexer #(.Bits(8)) multiplexer_8 (.sel(comparator_3_eq[1]), .in_0(Data_1), .in_1(multiplexer_4_out), .out(D_21));
  Multiplexer #(.Bits(8)) multiplexer_9 (.sel(comparator_4_eq[1]), .in_0(Data_2), .in_1(multiplexer_4_out), .out(D_22));
  Multiplexer #(.Bits(8)) multiplexer_10 (
    .sel(comparator_3_eq[0]), .in_0(Data_1), .in_1(multiplexer_5_out), .out(D_31));
  Multiplexer #(.Bits(8)) multiplexer_11 (
    .sel(comparator_4_eq[0]), .in_0(Data_2), .in_1(multiplexer_5_out), .out(D_32));
  Multiplexer #(.Selector_Bits(3), .Bits(8)) multiplexer_12 (
    .sel(comparator_3_eq), .in_0(Data_1), .in_1(D_31), .in_2(D_21), .in_3(D_21), .in_4(D_11), .in_5(D_11),
    .in_6(D_11), .in_7(D_11), .out(Out_1));
  Multiplexer #(.Selector_Bits(3), .Bits(8)) multiplexer_13 (
    .sel(comparator_4_eq), .in_0(Data_2), .in_1(D_32), .in_2(D_22), .in_3(D_22), .in_4(D_12), .in_5(D_12),
    .in_6(D_12), .in_7(D_12), .out(multiplexer_13_out));
  Multiplexer #(.Bits(8)) multiplexer_14 (.sel(IMM_Check), .in_0(multiplexer_13_out), .in_1(Data_2), .out(Out_2));
endmodule
