// Digital circuit multiplier.dig as structural Verilog
module multiplier (
  input  [7:0] A,
  input  CLK,
  input  [7:0] B,
  input  EN,
  output [7:0] M,
  output O_F
);

  wire comparator_1_eq, not_1_out, or_1_out, or_2_out;
  wire [7:0] _8bits_adder_1_s, counter_1_out, demultiplexer_1_out_0, demultiplexer_1_out_1,
       multiplexer_1_out, register_1_q;

  or or_1 (or_1_out, B[0], B[1], B[2], B[3], B[4], B[5], B[6], B[7]);
  or or_2 (or_2_out, or_1_out, EN);
  Comparator #(.Bits(8)) comparator_1 (.a(A), .b(counter_1_out), .eq(comparator_1_eq));  // open: gt, lt
  Counter #(.Bits(8)) counter_1 (.en(or_2_out), .C(CLK), .clr(comparator_1_eq), .out(counter_1_out));  // open: ovf
  _8bits_adder _8bits_adder_1 (.A(B), .B(demultiplexer_1_out_1), .C(1'b0), .S(_8bits_adder_1_s), .C_o(O_F));
  Multiplexer #(.Bits(8)) multiplexer_1 (
    .sel(comparator_1_eq), .in_0(_8bits_adder_1_s), .in_1({8{1'b0}}), .out(multiplexer_1_out));
  Demultiplexer #(.Bits(8)) demultiplexer_1 (
    .sel(not_1_out), .in(register_1_q), .out_0(demultiplexer_1_out_0), .out_1(demultiplexer_1_out_1));
  Multiplexer #(.Bits(8)) multiplexer_2 (.sel(EN), .in_0(demultiplexer_1_out_0), .in_1({8{1'b0}}), .out(M));
  not not_1 (not_1_out, comparator_1_eq);
  Register #(.Bits(8)) register_1 (.D(multiplexer_1_out), .C(CLK), .en(EN), .Q(register_1_q));

  // Notes on the sheet:
  //   A: default 4
  //   B: default 100
endmodule
